# Fritzing sketch Hardware (saved by Fritzing 0.9.3b)
breadboards: 1

parts:
  Onderdeel1 = Arduino Nano (Rev3.0)
  S1 = Pushbutton [package="[SMD]"]
  S2 = Pushbutton [package="[SMD]"]
  S3 = Pushbutton [package="[SMD]"]
  S4 = Pushbutton [package="[SMD]"]
  S5 = Pushbutton [package="[SMD]"]
  R1 = Rotary Potentiometer (Small) [maximum_resistance=100kΩ package=THT]
  J1 = Basic Servo
  J2 = Basic Servo
  J3 = Basic Servo
  J4 = Basic Servo
  J5 = Basic Servo

nets:
  GND: Onderdeel1.GND, S1.Pin_1, S1.Pin_2, S2.Pin_1, S2.Pin_2, S3.Pin_1, S3.Pin_2, S4.Pin_1, S4.Pin_2, S5.Pin_1, S5.Pin_2, R1.leg2, J1.gnd, J2.gnd, J3.gnd, J4.gnd, J5.gnd
  N1: Onderdeel1.D2, S1.Pin_3, S1.Pin_4
  N2: Onderdeel1.D3, S2.Pin_3, S2.Pin_4
  N3: Onderdeel1.D4, S3.Pin_3, S3.Pin_4
  N4: Onderdeel1.D5, S4.Pin_3, S4.Pin_4
  N5: Onderdeel1.D6, S5.Pin_3, S5.Pin_4
  N6: Onderdeel1.D8, J1.pulse
  N7: Onderdeel1.D9, J2.pulse
  N8: Onderdeel1.D10, J3.pulse
  N9: Onderdeel1.D11/MOSI, J4.pulse
  N10: Onderdeel1.D12/MISO, J5.pulse
  N11: Onderdeel1.5V, R1.leg1
  N12: Onderdeel1.A6, R1.wiper
